# Fritzing sketch arduino_breadboard (saved by Fritzing 0.9.5d)
breadboards: 1

parts:
  Bauteil2 = Arduino Nano (Rev3.0)
  Bauteil3 = Adafruit MCP4728
  Bauteil4 = Adafruit MCP4728

nets:
  GND: Bauteil2.GND, Bauteil3.GND, Bauteil4.GND
  N1: Bauteil2.D2, Bauteil4.!LDAC
  VCC: Bauteil2.5V, Bauteil3.VCC, Bauteil4.VCC
  N2: Bauteil2.A5, Bauteil3.SCL, Bauteil4.SCL
  N3: Bauteil2.A4, Bauteil3.SDA, Bauteil4.SDA

custom parts:
  Adafruit MCP4728: If you've ever said to yourself "Gee, I wish these four 12-bit DACs came in a single package with the ability to save their settings to an EEPROM", well I have good news. The MCP4728 is the answer to your wishes! Within it's little package, the MCP4728 has four, count em, four 12-bit DACs for whatever voltage setting needs you may have. In addition, it has the ability to store the settings for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
